// Logisim project circuito.circ as structural Verilog: 1 circuit, main circuit main
module main (
  input  in_1,
  input  in_2,
  input  in_3,
  input  in_4,
  input  enWrite,
  input  enRead,
  output out_7,
  output out_8,
  output out_9,
  output out_10
);

  wire and_1_out, clock_1_out, d_ff_1_q, d_ff_2_q, d_ff_3_q, d_ff_4_q;

  and and_1 (and_1_out, enWrite, clock_1_out);
  Clock clock_1 (.out(clock_1_out));
  D_Flip_Flop #(.trigger("falling")) d_ff_1 (.clk(and_1_out), .D(in_1), .Q(d_ff_1_q));  // open: Qn, preset, en, reset
  D_Flip_Flop #(.trigger("falling")) d_ff_2 (.clk(and_1_out), .D(in_2), .Q(d_ff_2_q));  // open: Qn, preset, en, reset
  D_Flip_Flop #(.trigger("falling")) d_ff_3 (.clk(and_1_out), .D(in_3), .Q(d_ff_3_q));  // open: Qn, preset, en, reset
  D_Flip_Flop #(.trigger("falling")) d_ff_4 (.clk(and_1_out), .D(in_4), .Q(d_ff_4_q));  // open: Qn, preset, en, reset
  assign out_7 = enRead ? d_ff_1_q : 1'bz;  // Controlled_Buffer controlled_buffer_1
  assign out_8 = enRead ? d_ff_2_q : 1'bz;  // Controlled_Buffer controlled_buffer_2
  assign out_9 = enRead ? d_ff_3_q : 1'bz;  // Controlled_Buffer controlled_buffer_3
  assign out_10 = enRead ? d_ff_4_q : 1'bz;  // Controlled_Buffer controlled_buffer_4
endmodule
