// Logisim project circuito_1.circ as structural Verilog: 1 circuit, main circuit main
module main (
  input  e0,
  input  e1,
  input  e2,
  input  e3,
  input  e3_2,
  input  enWrite,
  input  enRead,
  output out_8,
  output out_9,
  output out_10,
  output out_11,
  output out_12
);

  wire clock_1_out, d_ff_1_q, d_ff_2_q, d_ff_3_q, d_ff_4_q, d_ff_5_q;

  Clock clock_1 (.out(clock_1_out));
  D_Flip_Flop #(.trigger("falling")) d_ff_1 (
    .clk(clock_1_out), .D(e0), .Q(d_ff_1_q), .en(enWrite));  // open: Qn, preset, reset
  D_Flip_Flop #(.trigger("falling")) d_ff_2 (
    .clk(clock_1_out), .D(e1), .Q(d_ff_2_q), .en(enWrite));  // open: Qn, preset, reset
  D_Flip_Flop #(.trigger("falling")) d_ff_3 (
    .clk(clock_1_out), .D(e2), .Q(d_ff_3_q), .en(enWrite));  // open: Qn, preset, reset
  D_Flip_Flop #(.trigger("falling")) d_ff_4 (
    .clk(clock_1_out), .D(e3), .Q(d_ff_4_q), .en(enWrite));  // open: Qn, preset, reset
  D_Flip_Flop #(.trigger("falling")) d_ff_5 (
    .clk(clock_1_out), .D(e3_2), .Q(d_ff_5_q), .en(enWrite));  // open: Qn, preset, reset
  assign out_8 = enRead ? d_ff_1_q : 1'bz;  // Controlled_Buffer controlled_buffer_1
  assign out_9 = enRead ? d_ff_2_q : 1'bz;  // Controlled_Buffer controlled_buffer_2
  assign out_10 = enRead ? d_ff_3_q : 1'bz;  // Controlled_Buffer controlled_buffer_3
  assign out_11 = enRead ? d_ff_4_q : 1'bz;  // Controlled_Buffer controlled_buffer_4
  assign out_12 = enRead ? d_ff_5_q : 1'bz;  // Controlled_Buffer controlled_buffer_5

  // Notes on the sheet:
  //   Ejercicio 10. Incisos A y B
endmodule
