// Logisim project circuito_2.circ as structural Verilog: 1 circuit, main circuit main
module main (
  input  enWrite,
  input  enRead,
  output out_3,
  output out_4,
  output out_5,
  output out_6,
  output out_7
);

  wire clock_1_out, d_ff_1_q, d_ff_2_q, d_ff_3_q, d_ff_4_q, d_ff_5_q;

  Clock clock_1 (.out(clock_1_out));
  D_Flip_Flop #(.trigger("falling")) d_ff_1 (
    .clk(clock_1_out), .D(out_3), .Q(d_ff_1_q), .en(enWrite));  // open: Qn, preset, reset
  D_Flip_Flop #(.trigger("falling")) d_ff_2 (
    .clk(clock_1_out), .D(out_4), .Q(d_ff_2_q), .en(enWrite));  // open: Qn, preset, reset
  D_Flip_Flop #(.trigger("falling")) d_ff_3 (
    .clk(clock_1_out), .D(out_5), .Q(d_ff_3_q), .en(enWrite));  // open: Qn, preset, reset
  D_Flip_Flop #(.trigger("falling")) d_ff_4 (
    .clk(clock_1_out), .D(out_6), .Q(d_ff_4_q), .en(enWrite));  // open: Qn, preset, reset
  D_Flip_Flop #(.trigger("falling")) d_ff_5 (
    .clk(clock_1_out), .D(out_7), .Q(d_ff_5_q), .en(enWrite));  // open: Qn, preset, reset
  assign out_3 = enRead ? d_ff_1_q : 1'bz;  // Controlled_Buffer controlled_buffer_1
  assign out_4 = enRead ? d_ff_2_q : 1'bz;  // Controlled_Buffer controlled_buffer_2
  assign out_5 = enRead ? d_ff_3_q : 1'bz;  // Controlled_Buffer controlled_buffer_3
  assign out_6 = enRead ? d_ff_4_q : 1'bz;  // Controlled_Buffer controlled_buffer_4
  assign out_7 = enRead ? d_ff_5_q : 1'bz;  // Controlled_Buffer controlled_buffer_5

  // Notes on the sheet:
  //   Ejercicio 10. Inciso C
endmodule
