// Logisim project circuito_bis.circ as structural Verilog: 5 circuits, main circuit main
module main (
  input  enWrite,
  input  enRead,
  input  plus_1,
  input  plus_2,
  input  reset,
  output [7:0] out_6
);

  circuito_completo circuito_completo_1 (
    .reset(reset), .inc2(plus_2), .inc1(plus_1), .enRead(enRead), .enWrite(enWrite), .out_6(out_6));
endmodule

// 8_bit_reg
module _8_bit_register (
  input  [7:0] en,
  input  enWrite,
  input  enRead,
  output out_4,
  output out_5,
  output out_6,
  output out_7,
  output out_8,
  output out_9,
  output out_10,
  output out_11
);

  wire Clk_out, d_ff_1_q, d_ff_2_q, d_ff_3_q, d_ff_4_q, d_ff_5_q, d_ff_6_q, d_ff_7_q, d_ff_8_q;

  Clock Clk (.out(Clk_out));
  D_Flip_Flop #(.trigger("falling")) d_ff_1 (
    .clk(Clk_out), .D(en[0]), .Q(d_ff_1_q), .en(enWrite));  // open: Qn, preset, reset
  D_Flip_Flop #(.trigger("falling")) d_ff_2 (
    .clk(Clk_out), .D(en[1]), .Q(d_ff_2_q), .en(enWrite));  // open: Qn, preset, reset
  D_Flip_Flop #(.trigger("falling")) d_ff_3 (
    .clk(Clk_out), .D(en[2]), .Q(d_ff_3_q), .en(enWrite));  // open: Qn, preset, reset
  D_Flip_Flop #(.trigger("falling")) d_ff_4 (
    .clk(Clk_out), .D(en[3]), .Q(d_ff_4_q), .en(enWrite));  // open: Qn, preset, reset
  D_Flip_Flop #(.trigger("falling")) d_ff_5 (
    .clk(Clk_out), .D(en[4]), .Q(d_ff_5_q), .en(enWrite));  // open: Qn, preset, reset
  D_Flip_Flop #(.trigger("falling")) d_ff_6 (
    .clk(Clk_out), .D(en[5]), .Q(d_ff_6_q), .en(enWrite));  // open: Qn, preset, reset
  D_Flip_Flop #(.trigger("falling")) d_ff_7 (
    .clk(Clk_out), .D(en[6]), .Q(d_ff_7_q), .en(enWrite));  // open: Qn, preset, reset
  D_Flip_Flop #(.trigger("falling")) d_ff_8 (
    .clk(Clk_out), .D(en[7]), .Q(d_ff_8_q), .en(enWrite));  // open: Qn, preset, reset
  assign out_4 = enRead ? d_ff_1_q : 1'bz;  // Controlled_Buffer controlled_buffer_1
  assign out_5 = enRead ? d_ff_2_q : 1'bz;  // Controlled_Buffer controlled_buffer_2
  assign out_6 = enRead ? d_ff_3_q : 1'bz;  // Controlled_Buffer controlled_buffer_3
  assign out_7 = enRead ? d_ff_4_q : 1'bz;  // Controlled_Buffer controlled_buffer_4
  assign out_8 = enRead ? d_ff_5_q : 1'bz;  // Controlled_Buffer controlled_buffer_5
  assign out_9 = enRead ? d_ff_6_q : 1'bz;  // Controlled_Buffer controlled_buffer_6
  assign out_10 = enRead ? d_ff_7_q : 1'bz;  // Controlled_Buffer controlled_buffer_7
  assign out_11 = enRead ? d_ff_8_q : 1'bz;  // Controlled_Buffer controlled_buffer_8
endmodule

// sum
module sum_8_bits (
  input  [7:0] in_1,
  input  [7:0] in_2,
  output out_3,
  output out_4,
  output out_5,
  output out_6,
  output out_7,
  output out_8,
  output out_9,
  output out_10,
  output out_11
);

  wire complete_sum_2_carry, complete_sum_3_carry, complete_sum_4_carry, complete_sum_5_carry,
       complete_sum_6_carry, complete_sum_7_carry, complete_sum_8_carry;

  complete_sum complete_sum_1 (.in_1(in_1[7]), .in_2(in_2[7]), .carry(out_3), .num(out_4), .in_3(complete_sum_2_carry));
  complete_sum complete_sum_2 (
    .in_1(in_1[6]), .in_2(in_2[6]), .carry(complete_sum_2_carry), .num(out_5), .in_3(complete_sum_3_carry));
  complete_sum complete_sum_3 (
    .in_1(in_1[5]), .in_2(in_2[5]), .carry(complete_sum_3_carry), .num(out_6), .in_3(complete_sum_4_carry));
  complete_sum complete_sum_4 (
    .in_1(in_1[4]), .in_2(in_2[4]), .carry(complete_sum_4_carry), .num(out_7), .in_3(complete_sum_5_carry));
  complete_sum complete_sum_5 (
    .in_1(in_1[3]), .in_2(in_2[3]), .carry(complete_sum_5_carry), .num(out_8), .in_3(complete_sum_7_carry));
  complete_sum complete_sum_6 (
    .in_1(in_1[1]), .in_2(in_2[1]), .carry(complete_sum_6_carry), .num(out_10), .in_3(complete_sum_8_carry));
  complete_sum complete_sum_7 (
    .in_1(in_1[2]), .in_2(in_2[2]), .carry(complete_sum_7_carry), .num(out_9), .in_3(complete_sum_6_carry));
  complete_sum complete_sum_8 (.in_1(in_1[0]), .in_2(in_2[0]), .carry(complete_sum_8_carry), .num(out_11), .in_3(1'b0));
endmodule

module complete_sum (
  input  in_1,
  input  in_2,
  input  in_3,
  output carry,
  output num
);

  wire and_1_out, and_2_out, xor_2_out;

  or or_1 (carry, and_2_out, and_1_out);
  xor xor_1 (num, xor_2_out, in_3);
  and and_1 (and_1_out, xor_2_out, in_3);
  xor xor_2 (xor_2_out, in_1, in_2);
  and and_2 (and_2_out, in_1, in_2);
endmodule

module circuito_completo (
  input  enWrite,
  input  enRead,
  input  reset,
  input  inc2,
  input  inc1,
  output [7:0] out_6
);

  wire [1:0] and_1_out, and_2_out, and_3_out, bit_extender_1_out, bit_extender_2_out, bit_extender_3_out,
       or_1_out;
  wire [7:0] controlled_buffer_1_out, multiplexer_1_out, n8_bit_register_1_out_4, plus_1_out_11,
       plus_2_out_11;

  assign bit_extender_1_out = {{1{reset}}, reset};  // Bit_Extender bit_extender_1
  assign and_1_out = 2'b01 & bit_extender_1_out;  // AND_Gate and_1, 2 bits wide
  assign bit_extender_2_out = {{1{inc2}}, inc2};  // Bit_Extender bit_extender_2
  assign and_2_out = 2'b11 & bit_extender_2_out;  // AND_Gate and_2, 2 bits wide
  assign or_1_out = and_1_out | and_2_out | and_3_out;  // OR_Gate or_1, 2 bits wide
  assign bit_extender_3_out = {{1{inc1}}, inc1};  // Bit_Extender bit_extender_3
  assign and_3_out = 2'b10 & bit_extender_3_out;  // AND_Gate and_3, 2 bits wide
  sum_8_bits plus_2 (
    .in_1(8'h2), .in_2(n8_bit_register_1_out_4), .out_4(plus_2_out_11[7]), .out_5(plus_2_out_11[6]),
    .out_6(plus_2_out_11[5]), .out_7(plus_2_out_11[4]), .out_8(plus_2_out_11[3]), .out_9(plus_2_out_11[2]),
    .out_10(plus_2_out_11[1]), .out_11(plus_2_out_11[0]));  // open: out_3
  Multiplexer #(.select(2), .width(8)) multiplexer_1 (
    .in0(n8_bit_register_1_out_4), .in1({8{1'b0}}), .in2(plus_1_out_11), .in3(plus_2_out_11),
    .out(multiplexer_1_out), .sel(or_1_out));  // open: en
  assign controlled_buffer_1_out = enRead ? multiplexer_1_out : 8'bz;  // Controlled_Buffer controlled_buffer_1
  _8_bit_register u_8_bit_register_1 (
    .en(controlled_buffer_1_out), .enWrite(enWrite), .enRead(enRead), .out_4(n8_bit_register_1_out_4[0]),
    .out_5(n8_bit_register_1_out_4[1]), .out_6(n8_bit_register_1_out_4[2]),
    .out_7(n8_bit_register_1_out_4[3]), .out_8(n8_bit_register_1_out_4[4]),
    .out_9(n8_bit_register_1_out_4[5]), .out_10(n8_bit_register_1_out_4[6]),
    .out_11(n8_bit_register_1_out_4[7]));
  assign out_6 = enRead ? n8_bit_register_1_out_4 : 8'bz;  // Controlled_Buffer controlled_buffer_2
  sum_8_bits plus_1 (
    .in_1(n8_bit_register_1_out_4), .in_2(8'h1), .out_4(plus_1_out_11[7]), .out_5(plus_1_out_11[6]),
    .out_6(plus_1_out_11[5]), .out_7(plus_1_out_11[4]), .out_8(plus_1_out_11[3]), .out_9(plus_1_out_11[2]),
    .out_10(plus_1_out_11[1]), .out_11(plus_1_out_11[0]));  // open: out_3
endmodule
