// Logisim project multiplexor_3c.circ as structural Verilog: 2 circuits, main circuit main
module main (
  input  [7:0] in_1,
  input  [2:0] in_2,
  output out_3
);

  wire and_1_out, and_2_out, and_3_out, and_4_out, and_5_out, and_6_out, and_7_out, and_8_out, and_9_out,
       and_10_out, and_11_out, and_12_out, and_13_out, and_14_out, and_15_out, and_16_out, not_1_out,
       not_2_out, not_3_out;

  and and_1 (and_1_out, not_2_out, not_3_out, not_1_out);
  not not_1 (not_1_out, in_2[0]);
  not not_2 (not_2_out, in_2[2]);
  not not_3 (not_3_out, in_2[1]);
  and and_2 (and_2_out, and_1_out, in_1[0]);
  and and_3 (and_3_out, in_1[1], and_5_out);
  and and_4 (and_4_out, not_2_out, in_2[1], not_1_out);
  and and_5 (and_5_out, not_2_out, not_3_out, in_2[0]);
  and and_6 (and_6_out, in_1[2], and_4_out);
  and and_7 (and_7_out, not_2_out, in_2[0], in_2[1]);
  and and_8 (and_8_out, in_1[3], and_7_out);
  and and_9 (and_9_out, in_2[2], not_3_out, not_1_out);
  and and_10 (and_10_out, in_1[4], and_9_out);
  and and_11 (and_11_out, in_1[5], and_12_out);
  and and_12 (and_12_out, in_2[2], not_3_out, in_2[0]);
  and and_13 (and_13_out, in_2[2], in_2[1], not_1_out);
  and and_14 (and_14_out, in_1[6], and_13_out);
  and and_15 (and_15_out, in_2[2], in_2[1], in_2[0]);
  and and_16 (and_16_out, in_1[7], and_15_out);
  or or_1 (out_3, and_2_out, and_3_out, and_6_out, and_8_out, and_10_out, and_11_out, and_14_out, and_16_out);
endmodule

module mux_3c (
  input  [7:0] in_1,
  input  [2:0] in_2,
  output out_3
);

  wire and_1_out, and_2_out, and_3_out, and_4_out, and_5_out, and_6_out, and_7_out, and_8_out, and_9_out,
       and_10_out, and_11_out, and_12_out, and_13_out, and_14_out, and_15_out, and_16_out, not_1_out,
       not_2_out, not_3_out;

  and and_1 (and_1_out, not_3_out, not_2_out, not_1_out);
  not not_1 (not_1_out, in_2[0]);
  not not_2 (not_2_out, in_2[1]);
  not not_3 (not_3_out, in_2[2]);
  and and_2 (and_2_out, and_1_out, in_1[0]);
  and and_3 (and_3_out, in_1[1], and_4_out);
  and and_4 (and_4_out, not_3_out, not_2_out, in_2[0]);
  and and_5 (and_5_out, in_1[2], and_7_out);
  and and_6 (and_6_out, not_3_out, in_2[0], in_2[1]);
  and and_7 (and_7_out, not_3_out, in_2[1], not_1_out);
  and and_8 (and_8_out, in_1[3], and_6_out);
  and and_9 (and_9_out, in_2[2], not_2_out, not_1_out);
  and and_10 (and_10_out, in_1[4], and_9_out);
  and and_11 (and_11_out, in_2[2], not_2_out, in_2[0]);
  and and_12 (and_12_out, in_1[5], and_11_out);
  and and_13 (and_13_out, in_1[6], and_14_out);
  and and_14 (and_14_out, in_2[2], in_2[1], not_1_out);
  and and_15 (and_15_out, in_2[2], in_2[1], in_2[0]);
  and and_16 (and_16_out, in_1[7], and_15_out);
  or or_1 (out_3, and_2_out, and_3_out, and_5_out, and_8_out, and_10_out, and_12_out, and_13_out, and_16_out);
endmodule
