// Logisim project multiplexor_3c_prebuilt.circ as structural Verilog: 2 circuits, main circuit main
module main (
  input  [7:0] in_1,
  input  [2:0] in_2,
  output out_3
);

  Multiplexer #(.select(3), .disabled(0), .enable("false")) multiplexer_1 (
    .in0(in_1[0]), .in1(in_1[1]), .in2(in_1[2]), .in3(in_1[3]), .in4(in_1[4]), .in5(in_1[5]), .in6(in_1[6]),
    .in7(in_1[7]), .out(out_3), .sel(in_2));
endmodule

module mux_3c (
  input  [7:0] in_1,
  input  [2:0] in_2,
  output out_3
);

  Multiplexer #(.select(3), .disabled(0), .enable("false")) multiplexer_1 (
    .in0(in_1[0]), .in1(in_1[1]), .in2(in_1[2]), .in3(in_1[3]), .in4(in_1[4]), .in5(in_1[5]), .in6(in_1[6]),
    .in7(in_1[7]), .out(out_3), .sel(in_2));
endmodule
