// Logisim project swapper_circuit.circ as structural Verilog: 1 circuit, main circuit main
module main (
  input  [1:0] e0_and_e1,
  input  C,
  output S1,
  output S0
);

  wire and_1_out, and_2_out, and_3_out, and_4_out, not_1_out;

  and and_1 (and_1_out, e0_and_e1[0], C);
  and and_2 (and_2_out, e0_and_e1[0], not_1_out);
  and and_3 (and_3_out, C, e0_and_e1[1]);
  and and_4 (and_4_out, not_1_out, e0_and_e1[1]);
  not not_1 (not_1_out, C);
  or or_1 (S0, and_2_out, and_3_out);
  or or_2 (S1, and_1_out, and_4_out);
endmodule
