// Logisim project swapper_mux_circuit.circ as structural Verilog: 1 circuit, main circuit main
module main (
  input  [1:0] Entradas,
  input  in_2,
  output S0,
  output S1
);

  Multiplexer #(.enable("false")) multiplexer_1 (.in0(Entradas[0]), .in1(Entradas[1]), .out(S0), .sel(in_2));
  Multiplexer #(.enable("false")) multiplexer_2 (.in0(Entradas[1]), .in1(Entradas[0]), .out(S1), .sel(in_2));
endmodule
