// Logisim project decoder_only_or.circ as structural Verilog: 1 circuit, main circuit main
module main (
  input  [2:0] in_1,
  output out_2
);

  wire decoder_1_out0, decoder_1_out1, decoder_1_out2, decoder_1_out3, decoder_1_out4, decoder_1_out5,
       decoder_1_out6, decoder_1_out7, or_1_out, or_2_out;

  Decoder #(.select(3)) decoder_1 (
    .out0(decoder_1_out0), .out1(decoder_1_out1), .out2(decoder_1_out2), .out3(decoder_1_out3),
    .out4(decoder_1_out4), .out5(decoder_1_out5), .out6(decoder_1_out6), .out7(decoder_1_out7), .sel(in_1));  // open: en
  or or_1 (or_1_out, decoder_1_out0, decoder_1_out2);
  or or_2 (or_2_out, decoder_1_out4, decoder_1_out7);
  or or_3 (out_2, or_1_out, or_2_out);
endmodule
