// Logisim project solo_nand_nor.circ as structural Verilog: 1 circuit, main circuit main
module main (
  input  A,
  input  B,
  input  C,
  output F
);

  wire nand_1_out, nor_1_out, nor_2_out, not_1_out, not_2_out, not_3_out, not_4_out, not_5_out, not_6_out;

  nor nor_1 (nor_1_out, A, B, C);
  not not_1 (not_1_out, A);
  not not_2 (not_2_out, B);
  nand nand_1 (nand_1_out, not_1_out, not_2_out);
  not not_3 (not_3_out, nand_1_out);
  not not_4 (not_4_out, C);
  not not_5 (not_5_out, nor_1_out);
  nor nor_2 (nor_2_out, not_3_out, not_4_out);
  not not_6 (not_6_out, nor_2_out);
  nand nand_2 (F, not_5_out, not_6_out);
endmodule
