// Logisim project circuito_x3.circ as structural Verilog: 3 circuits, main circuit main
module main (
  input  [4:0] in_1,
  input  in_2,
  output out_3,
  output [7:0] out_4
);

  mult_x3 mult_x3_1 (.out_3(out_3), .in_1(in_1), .out_4(out_4), .in_2(in_2));
endmodule

// SUM
module sum_completo (
  input  in_1,
  input  in_2,
  input  in_3,
  output out_4,
  output out_5
);

  wire and_1_out, and_2_out, xor_1_out;

  and and_1 (and_1_out, xor_1_out, in_3);
  or or_1 (out_4, and_2_out, and_1_out);
  xor xor_1 (xor_1_out, in_1, in_2);
  xor xor_2 (out_5, xor_1_out, in_3);
  and and_2 (and_2_out, in_1, in_2);
endmodule

module mult_x3 (
  input  [4:0] in_1,
  input  in_2,
  output out_3,
  output [7:0] out_4
);

  wire sum_completo_1_out_4, sum_completo_1_out_5, sum_completo_3_out_4, sum_completo_3_out_5,
       sum_completo_4_out_4, sum_completo_5_out_4, sum_completo_5_out_5, sum_completo_6_out_4,
       sum_completo_7_out_4, sum_completo_7_out_5, sum_completo_8_out_4, sum_completo_9_out_4,
       sum_completo_9_out_5, sum_completo_10_out_4, sum_completo_11_out_4, sum_completo_11_out_5,
       sum_completo_12_out_4, sum_completo_12_out_5, sum_completo_13_out_4, sum_completo_14_out_4,
       sum_completo_15_out_4, sum_completo_15_out_5, sum_completo_16_out_4;
  wire [7:0] bit_extender_1_out;

  sum_completo sum_completo_1 (
    .in_1(bit_extender_1_out[7]), .in_2(bit_extender_1_out[7]), .out_4(sum_completo_1_out_4),
    .out_5(sum_completo_1_out_5), .in_3(sum_completo_3_out_4));
  sum_completo sum_completo_2 (
    .in_1(bit_extender_1_out[7]), .in_2(sum_completo_1_out_5), .out_4(out_3), .out_5(out_4[7]),
    .in_3(sum_completo_4_out_4));
  sum_completo sum_completo_3 (
    .in_1(bit_extender_1_out[6]), .in_2(bit_extender_1_out[6]), .out_4(sum_completo_3_out_4),
    .out_5(sum_completo_3_out_5), .in_3(sum_completo_5_out_4));
  sum_completo sum_completo_4 (
    .in_1(bit_extender_1_out[6]), .in_2(sum_completo_3_out_5), .out_4(sum_completo_4_out_4),
    .out_5(out_4[6]), .in_3(sum_completo_6_out_4));
  sum_completo sum_completo_5 (
    .in_1(bit_extender_1_out[5]), .in_2(bit_extender_1_out[5]), .out_4(sum_completo_5_out_4),
    .out_5(sum_completo_5_out_5), .in_3(sum_completo_7_out_4));
  sum_completo sum_completo_6 (
    .in_1(bit_extender_1_out[5]), .in_2(sum_completo_5_out_5), .out_4(sum_completo_6_out_4),
    .out_5(out_4[5]), .in_3(sum_completo_8_out_4));
  sum_completo sum_completo_7 (
    .in_1(bit_extender_1_out[4]), .in_2(bit_extender_1_out[4]), .out_4(sum_completo_7_out_4),
    .out_5(sum_completo_7_out_5), .in_3(sum_completo_9_out_4));
  sum_completo sum_completo_8 (
    .in_1(bit_extender_1_out[4]), .in_2(sum_completo_7_out_5), .out_4(sum_completo_8_out_4),
    .out_5(out_4[4]), .in_3(sum_completo_10_out_4));
  sum_completo sum_completo_9 (
    .in_1(bit_extender_1_out[3]), .in_2(bit_extender_1_out[3]), .out_4(sum_completo_9_out_4),
    .out_5(sum_completo_9_out_5), .in_3(sum_completo_11_out_4));
  sum_completo sum_completo_10 (
    .in_1(bit_extender_1_out[3]), .in_2(sum_completo_9_out_5), .out_4(sum_completo_10_out_4),
    .out_5(out_4[3]), .in_3(sum_completo_13_out_4));
  assign bit_extender_1_out = {{3{1'b0}}, in_1};  // Bit_Extender bit_extender_1
  sum_completo sum_completo_11 (
    .in_1(bit_extender_1_out[2]), .in_2(bit_extender_1_out[2]), .out_4(sum_completo_11_out_4),
    .out_5(sum_completo_11_out_5), .in_3(sum_completo_12_out_4));
  sum_completo sum_completo_12 (
    .in_1(bit_extender_1_out[1]), .in_2(bit_extender_1_out[1]), .out_4(sum_completo_12_out_4),
    .out_5(sum_completo_12_out_5), .in_3(sum_completo_15_out_4));
  sum_completo sum_completo_13 (
    .in_1(bit_extender_1_out[2]), .in_2(sum_completo_11_out_5), .out_4(sum_completo_13_out_4),
    .out_5(out_4[2]), .in_3(sum_completo_14_out_4));
  sum_completo sum_completo_14 (
    .in_1(bit_extender_1_out[1]), .in_2(sum_completo_12_out_5), .out_4(sum_completo_14_out_4),
    .out_5(out_4[1]), .in_3(sum_completo_16_out_4));
  sum_completo sum_completo_15 (
    .in_1(bit_extender_1_out[0]), .in_2(bit_extender_1_out[0]), .out_4(sum_completo_15_out_4),
    .out_5(sum_completo_15_out_5), .in_3(in_2));
  sum_completo sum_completo_16 (
    .in_1(bit_extender_1_out[0]), .in_2(sum_completo_15_out_5), .out_4(sum_completo_16_out_4),
    .out_5(out_4[0]), .in_3(sum_completo_1_out_4));
endmodule
