// Logisim project circuito.circ as structural Verilog: 3 circuits, main circuit main
module main (
  input  in_1,
  input  [5:0] in_2,
  output out_3,
  output out_4,
  output out_5,
  output out_6,
  output out_7,
  output out_8,
  output out_9
);

  dispositivo dispositivo_1 (
    .in_2(in_1), .in_1(in_2[5]), .in_3(in_2[4]), .in_4(in_2[3]), .in_5(in_2[2]), .in_6(in_2[1]),
    .in_7(in_2[0]), .out_14(out_8), .out_8(out_9), .out_9(out_5), .out_10(out_6), .out_11(out_7),
    .out_12(out_3), .out_13(out_4));
endmodule

// SUM
module sum_completo (
  input  in_1,
  input  in_2,
  input  in_3,
  output out_4,
  output out_5
);

  wire and_1_out, and_2_out, xor_2_out;

  or or_1 (out_4, and_2_out, and_1_out);
  and and_1 (and_1_out, xor_2_out, in_3);
  xor xor_1 (out_5, xor_2_out, in_3);
  xor xor_2 (xor_2_out, in_1, in_2);
  and and_2 (and_2_out, in_1, in_2);
endmodule

module dispositivo (
  input  in_1,
  input  in_2,
  input  in_3,
  input  in_4,
  input  in_5,
  input  in_6,
  input  in_7,
  output out_8,
  output out_9,
  output out_10,
  output out_11,
  output out_12,
  output out_13,
  output out_14
);

  wire not_1_out, not_3_out, not_4_out, not_5_out, not_6_out, not_7_out, not_8_out, pull_resistor_1_node,
       pull_resistor_2_node, pull_resistor_3_node, pull_resistor_4_node, pull_resistor_5_node,
       pull_resistor_6_node, sum_completo_1_out_4, sum_completo_1_out_5, sum_completo_2_out_4,
       sum_completo_2_out_5, sum_completo_3_out_4, sum_completo_3_out_5, sum_completo_4_out_4,
       sum_completo_4_out_5, sum_completo_5_out_4, sum_completo_5_out_5, sum_completo_6_out_4,
       sum_completo_6_out_5, xor_1_out, xor_2_out;

  xor xor_1 (xor_1_out, pull_resistor_1_node, not_3_out);
  not not_1 (not_1_out, xor_1_out);
  xor xor_2 (xor_2_out, not_1_out, sum_completo_2_out_4);
  not not_2 (out_14, xor_2_out);
  Pull_Resistor pull_resistor_1 (.node(pull_resistor_1_node));
  not not_3 (not_3_out, in_1);
  sum_completo sum_completo_1 (
    .in_1(pull_resistor_1_node), .in_2(not_3_out), .out_4(sum_completo_1_out_4),
    .out_5(sum_completo_1_out_5), .in_3(sum_completo_2_out_4));
  and and_1 (out_8, in_2, sum_completo_1_out_5);
  Pull_Resistor pull_resistor_2 (.node(pull_resistor_2_node));
  not not_4 (not_4_out, in_3);
  sum_completo sum_completo_2 (
    .in_1(pull_resistor_2_node), .in_2(not_4_out), .out_4(sum_completo_2_out_4),
    .out_5(sum_completo_2_out_5), .in_3(sum_completo_3_out_4));
  and and_2 (out_9, in_2, sum_completo_2_out_5);
  Pull_Resistor pull_resistor_3 (.node(pull_resistor_3_node));
  not not_5 (not_5_out, in_4);
  sum_completo sum_completo_3 (
    .in_1(pull_resistor_3_node), .in_2(not_5_out), .out_4(sum_completo_3_out_4),
    .out_5(sum_completo_3_out_5), .in_3(sum_completo_4_out_4));
  and and_3 (out_10, in_2, sum_completo_3_out_5);
  Pull_Resistor pull_resistor_4 (.node(pull_resistor_4_node));
  not not_6 (not_6_out, in_5);
  and and_4 (out_11, in_2, sum_completo_4_out_5);
  Pull_Resistor pull_resistor_5 (.node(pull_resistor_5_node));
  sum_completo sum_completo_4 (
    .in_1(pull_resistor_4_node), .in_2(not_6_out), .out_4(sum_completo_4_out_4),
    .out_5(sum_completo_4_out_5), .in_3(sum_completo_5_out_4));
  and and_5 (out_12, in_2, sum_completo_5_out_5);
  not not_7 (not_7_out, in_6);
  sum_completo sum_completo_5 (
    .in_1(pull_resistor_5_node), .in_2(not_7_out), .out_4(sum_completo_5_out_4),
    .out_5(sum_completo_5_out_5), .in_3(sum_completo_6_out_4));
  Pull_Resistor pull_resistor_6 (.node(pull_resistor_6_node));
  not not_8 (not_8_out, in_7);
  sum_completo sum_completo_6 (
    .in_1(pull_resistor_6_node), .in_2(not_8_out), .out_4(sum_completo_6_out_4),
    .out_5(sum_completo_6_out_5), .in_3(1'b1));
  and and_6 (out_13, in_2, sum_completo_6_out_5);
endmodule
