// Logisim project circuito.circ as structural Verilog: 3 circuits, main circuit main
module main (
);

  alu alu_1 ();  // open: in_3, in_1, in_2, out_6, out_7, out_8, out_9, Carry, Zero, Negative, Overflow
endmodule

// SUM
module sumador (
  input  in_1,
  input  in_2,
  input  in_3,
  output out_4,
  output out_5
);

  wire and_1_out, and_2_out, xor_2_out;

  or or_1 (out_4, and_2_out, and_1_out);
  and and_1 (and_1_out, in_3, xor_2_out);
  xor xor_1 (out_5, xor_2_out, in_3);
  and and_2 (and_2_out, in_1, in_2);
  xor xor_2 (xor_2_out, in_1, in_2);
endmodule

// ALU
module alu (
  input  [3:0] in_1,
  input  [3:0] in_2,
  input  in_3,
  output Carry,
  output Zero,
  output out_6,
  output out_7,
  output out_8,
  output out_9,
  output Negative,
  output Overflow
);

  wire not_1_out, not_2_out, not_3_out, not_4_out, not_5_out, sumador_2_out_4, sumador_3_out_4,
       sumador_4_out_4, xor_2_out, xor_3_out, xor_4_out, xor_5_out;

  xor xor_1 (Overflow, sumador_2_out_4, Carry);
  xor xor_2 (xor_2_out, in_3, in_2[3]);
  sumador sumador_1 (.in_1(in_1[3]), .in_2(xor_2_out), .out_4(Carry), .out_5(out_6), .in_3(sumador_2_out_4));
  xor xor_3 (xor_3_out, in_3, in_2[2]);
  sumador sumador_2 (.in_1(in_1[2]), .in_2(xor_3_out), .out_4(sumador_2_out_4), .out_5(out_7), .in_3(sumador_3_out_4));
  xor xor_4 (xor_4_out, in_3, in_2[1]);
  sumador sumador_3 (.in_1(in_1[1]), .in_2(xor_4_out), .out_4(sumador_3_out_4), .out_5(out_8), .in_3(sumador_4_out_4));
  xor xor_5 (xor_5_out, in_3, in_2[0]);
  sumador sumador_4 (.in_1(in_1[0]), .in_2(xor_5_out), .out_4(sumador_4_out_4), .out_5(out_9), .in_3(in_3));
  not not_1 (not_1_out, Carry);
  not not_2 (not_2_out, out_9);
  not not_3 (not_3_out, out_8);
  and and_1 (Zero, not_1_out, not_2_out, not_3_out, not_4_out, not_5_out);
  not not_4 (not_4_out, out_7);
  not not_5 (not_5_out, out_6);

  assign Negative = Carry;
endmodule
