// Logisim project alu.circ as structural Verilog: 7 circuits, main circuit main
// SUM
module main (
  input  [4:0] A,
  input  [4:0] B,
  input  [1:0] BITS_CONTROL,
  input  [4:0] SALIDA,
  output CARRY,
  output ZERO,
  output CARRY_OUT
);

  alu_2c alu_2c_1 (
    .in_3(BITS_CONTROL), .A(A), .B(B), .out_7(SALIDA), .CARRY(CARRY), .ZERO(ZERO), .CARRY_OUT(CARRY_OUT));

  // Notes on the sheet:
  //   00 --> SUMA
  //   01 --> RESTA
  //   10 --> NEG. A
  //   11 --> NEG. B
endmodule

// SUM
module complete_sum (
  input  in_1,
  input  in_2,
  input  in_3,
  output out_4,
  output out_5
);

  wire and_1_out, and_2_out, xor_2_out;

  xor xor_1 (out_4, xor_2_out, in_3);
  or or_1 (out_5, and_2_out, and_1_out);
  and and_1 (and_1_out, xor_2_out, in_3);
  xor xor_2 (xor_2_out, in_1, in_2);
  and and_2 (and_2_out, in_1, in_2);
endmodule

// SUM_5_BITS
module sum_5_bits (
  input  in_1,
  input  in_2,
  input  in_3,
  input  in_4,
  input  in_5,
  input  in_6,
  input  in_7,
  input  in_8,
  input  in_9,
  input  in_10,
  input  in_11,
  output out_12,
  output out_13,
  output out_14,
  output out_15,
  output out_16,
  output out_17,
  output out_18,
  output out_19
);

  wire complete_sum_2_out_5, complete_sum_3_out_5, complete_sum_4_out_5, complete_sum_5_out_5, not_1_out,
       not_2_out, not_3_out, not_4_out, not_5_out, not_6_out;

  and and_1 (out_13, not_1_out, not_2_out, not_3_out, not_4_out, not_5_out, not_6_out);
  not not_1 (not_1_out, out_18);
  not not_2 (not_2_out, out_17);
  not not_3 (not_3_out, out_16);
  not not_4 (not_4_out, out_15);
  not not_5 (not_5_out, out_14);
  not not_6 (not_6_out, out_12);
  complete_sum complete_sum_1 (.in_1(in_1), .in_2(in_2), .out_5(out_12), .out_4(out_14), .in_3(complete_sum_2_out_5));
  complete_sum complete_sum_2 (
    .in_1(in_3), .in_2(in_4), .out_5(complete_sum_2_out_5), .out_4(out_15), .in_3(complete_sum_3_out_5));
  complete_sum complete_sum_3 (
    .in_1(in_5), .in_2(in_6), .out_5(complete_sum_3_out_5), .out_4(out_16), .in_3(complete_sum_4_out_5));
  complete_sum complete_sum_4 (
    .in_1(in_7), .in_2(in_8), .out_5(complete_sum_4_out_5), .out_4(out_17), .in_3(complete_sum_5_out_5));
  complete_sum complete_sum_5 (.in_1(in_9), .in_2(in_10), .out_5(complete_sum_5_out_5), .out_4(out_18), .in_3(in_11));

  assign out_19 = out_12;
endmodule

// SUM TEST
module sum_test (
  input  [4:0] in_1,
  input  [4:0] in_2,
  input  in_3,
  output out_4,
  output out_5,
  output out_6,
  output out_7,
  output out_8,
  output out_9,
  output out_10,
  output out_11
);

  wire complete_sum_2_out_5, complete_sum_3_out_5, complete_sum_4_out_5, complete_sum_5_out_5, not_1_out,
       not_2_out, not_3_out, not_4_out, not_5_out, not_6_out;

  and and_1 (out_5, not_1_out, not_2_out, not_3_out, not_4_out, not_5_out, not_6_out);
  not not_1 (not_1_out, out_10);
  not not_2 (not_2_out, out_9);
  not not_3 (not_3_out, out_8);
  not not_4 (not_4_out, out_7);
  not not_5 (not_5_out, out_6);
  not not_6 (not_6_out, out_4);
  complete_sum complete_sum_1 (
    .in_1(in_1[4]), .in_2(in_2[4]), .out_5(out_4), .out_4(out_6), .in_3(complete_sum_2_out_5));
  complete_sum complete_sum_2 (
    .in_1(in_1[3]), .in_2(in_2[3]), .out_5(complete_sum_2_out_5), .out_4(out_7), .in_3(complete_sum_3_out_5));
  complete_sum complete_sum_3 (
    .in_1(in_1[2]), .in_2(in_2[2]), .out_5(complete_sum_3_out_5), .out_4(out_8), .in_3(complete_sum_4_out_5));
  complete_sum complete_sum_4 (
    .in_1(in_1[1]), .in_2(in_2[1]), .out_5(complete_sum_4_out_5), .out_4(out_9), .in_3(complete_sum_5_out_5));
  complete_sum complete_sum_5 (
    .in_1(in_1[0]), .in_2(in_2[0]), .out_5(complete_sum_5_out_5), .out_4(out_10), .in_3(in_3));

  assign out_11 = out_4;
endmodule

// SUM/RESTADOR
module sum_restador (
  input  in_1,
  input  in_2,
  input  in_3,
  input  in_4,
  input  in_5,
  input  in_6,
  input  in_7,
  input  in_8,
  input  in_9,
  input  in_10,
  input  in_11,
  output out_12,
  output out_13,
  output out_14,
  output out_15,
  output out_16,
  output out_17,
  output out_18,
  output out_19
);

  wire xor_1_out, xor_2_out, xor_3_out, xor_4_out, xor_5_out;

  xor xor_1 (xor_1_out, in_1, in_11);
  xor xor_2 (xor_2_out, in_4, in_11);
  xor xor_3 (xor_3_out, in_8, in_11);
  xor xor_4 (xor_4_out, in_6, in_11);
  sum_5_bits sum_5_bits_1 (
    .out_12(out_12), .out_13(out_13), .in_1(in_2), .in_2(xor_1_out), .in_3(in_3), .in_4(xor_2_out),
    .in_5(in_5), .in_6(xor_4_out), .in_7(in_7), .in_8(xor_3_out), .in_9(in_9), .in_10(xor_5_out),
    .out_19(out_14), .out_14(out_15), .out_15(out_16), .out_16(out_17), .out_17(out_18), .out_18(out_19),
    .in_11(in_11));
  xor xor_5 (xor_5_out, in_10, in_11);
endmodule

// NOT
module \not  (
  input  [4:0] in_1,
  output [4:0] out_2
);

  assign out_2 = ~in_1;  // NOT_Gate not_1, 5 bits wide
endmodule

// ALU
module alu_2c (
  input  [4:0] A,
  input  [4:0] B,
  input  [1:0] in_3,
  output CARRY,
  output ZERO,
  output CARRY_OUT,
  output [4:0] out_7
);

  wire and_1_out, and_2_out, and_3_out, and_4_out, and_7_out, not_1_out, not_2_out, not_4_out;
  wire [4:0] and_5_out, and_6_out, and_8_out, bit_extender_1_out, bit_extender_2_out, bit_extender_3_out,
       bit_extender_4_out, not_3_out_2, not_5_out_2, or_2_out, sum_restador_1_out_19;

  not not_1 (not_1_out, in_3[0]);
  not not_2 (not_2_out, in_3[1]);
  and and_1 (and_1_out, not_1_out, not_2_out);
  and and_2 (and_2_out, in_3[0], not_2_out);
  and and_3 (and_3_out, not_1_out, in_3[1]);
  and and_4 (and_4_out, in_3[1], in_3[0]);
  assign and_5_out = bit_extender_1_out & not_3_out_2;  // AND_Gate and_5, 5 bits wide
  assign bit_extender_1_out = {{4{and_3_out}}, and_3_out};  // Bit_Extender bit_extender_1
  assign bit_extender_2_out = {{4{and_4_out}}, and_4_out};  // Bit_Extender bit_extender_2
  \not  not_3 (.in_1(A), .out_2(not_3_out_2));
  assign bit_extender_3_out = {{4{1'b1}}, and_2_out};  // Bit_Extender bit_extender_3
  assign out_7 = and_5_out | and_6_out | and_8_out;  // OR_Gate or_1, 5 bits wide
  sum_restador sum_restador_1 (
    .out_12(CARRY), .out_13(ZERO), .in_2(A[4]), .in_1(B[4]), .in_3(A[3]), .in_4(B[3]), .in_5(A[2]),
    .in_6(B[2]), .in_7(A[1]), .in_8(B[1]), .in_9(A[0]), .in_10(B[0]), .out_14(CARRY_OUT),
    .out_15(sum_restador_1_out_19[4]), .out_16(sum_restador_1_out_19[3]), .out_17(sum_restador_1_out_19[2]),
    .out_18(sum_restador_1_out_19[1]), .out_19(sum_restador_1_out_19[0]), .in_11(and_7_out));
  assign bit_extender_4_out = {{4{1'b1}}, and_1_out};  // Bit_Extender bit_extender_4
  assign or_2_out = bit_extender_3_out | bit_extender_4_out;  // OR_Gate or_2, 5 bits wide
  assign and_6_out = or_2_out & sum_restador_1_out_19;  // AND_Gate and_6, 5 bits wide
  and and_7 (and_7_out, not_4_out, and_2_out);
  not not_4 (not_4_out, and_1_out);
  \not  not_5 (.in_1(B), .out_2(not_5_out_2));
  assign and_8_out = bit_extender_2_out & not_5_out_2;  // AND_Gate and_8, 5 bits wide
endmodule
